// Logisim project ProiectFDBargaoanuBogdan.circ as structural Verilog: 1 circuit, main circuit main
module main (
  input  A,
  input  B,
  input  C,
  input  D,
  input  E,
  output out_6
);

  wire and_1_out, and_2_out, nand_1_out;

  nand nand_1 (nand_1_out, A, B, C);
  and and_1 (and_1_out, C, D, E);
  and and_2 (and_2_out, nand_1_out, and_1_out);
  nor nor_1 (out_6, A, nand_1_out, and_2_out);

  // Notes on the sheet:
  //   F
  //   G
  //   H
  //   I
  //   K
  //   L
  //   J
  //   M
  //   Z
endmodule
